// Logisim project bit_shifter.circ as structural Verilog: 1 circuit, main circuit main
module main (
  input  [15:0] in,
  input  left_or_right,
  output [15:0] shift_result
);

  Multiplexer #(.enable("false")) multiplexer_1 (.in0(in[14]), .in1(1'b0), .out(shift_result[15]), .sel(left_or_right));
  Multiplexer #(.enable("false")) multiplexer_2 (
    .in0(in[13]), .in1(in[15]), .out(shift_result[14]), .sel(left_or_right));
  Multiplexer #(.enable("false")) multiplexer_3 (
    .in0(in[12]), .in1(in[14]), .out(shift_result[13]), .sel(left_or_right));
  Multiplexer #(.enable("false")) multiplexer_4 (
    .in0(in[11]), .in1(in[13]), .out(shift_result[12]), .sel(left_or_right));
  Multiplexer #(.enable("false")) multiplexer_5 (
    .in0(in[10]), .in1(in[12]), .out(shift_result[11]), .sel(left_or_right));
  Multiplexer #(.enable("false")) multiplexer_6 (
    .in0(in[9]), .in1(in[11]), .out(shift_result[10]), .sel(left_or_right));
  Multiplexer #(.enable("false")) multiplexer_7 (.in0(in[8]), .in1(in[10]), .out(shift_result[9]), .sel(left_or_right));
  Multiplexer #(.enable("false")) multiplexer_8 (.in0(in[7]), .in1(in[9]), .out(shift_result[8]), .sel(left_or_right));
  Multiplexer #(.enable("false")) multiplexer_9 (.in0(in[6]), .in1(in[8]), .out(shift_result[7]), .sel(left_or_right));
  Multiplexer #(.enable("false")) multiplexer_10 (.in0(in[5]), .in1(in[7]), .out(shift_result[6]), .sel(left_or_right));
  Multiplexer #(.enable("false")) multiplexer_11 (.in0(in[4]), .in1(in[6]), .out(shift_result[5]), .sel(left_or_right));
  Multiplexer #(.enable("false")) multiplexer_12 (.in0(in[3]), .in1(in[5]), .out(shift_result[4]), .sel(left_or_right));
  Multiplexer #(.enable("false")) multiplexer_13 (.in0(in[2]), .in1(in[4]), .out(shift_result[3]), .sel(left_or_right));
  Multiplexer #(.enable("false")) multiplexer_14 (.in0(in[1]), .in1(in[3]), .out(shift_result[2]), .sel(left_or_right));
  Multiplexer #(.enable("false")) multiplexer_15 (.in0(in[0]), .in1(in[2]), .out(shift_result[1]), .sel(left_or_right));
  Multiplexer #(.enable("false")) multiplexer_16 (.in0(1'b0), .in1(in[1]), .out(shift_result[0]), .sel(left_or_right));
endmodule
